# Fritzing sketch STMpel_DAC8734 (saved by Fritzing 0.9.1b)
breadboards: 1

parts:
  U1 = SSOP48 [chip_label=DAC8734 part_number=DAC8734 package=SSOP]
  R1 = Resistor [tolerance=±5% resistance=1k package=THT]

nets:
  CS: U1.2
  SCLK: U1.3
  MOSI: U1.4
  MISO: U1.5
  GND: U1.6, U1.10, U1.11, U1.18, U1.20, U1.27, U1.29, U1.32, U1.41, U1.43, U1.48
  N1: U1.7, R1.Pin_1
  IO_Vdd: U1.13
  5V: U1.14, R1.Pin_0
  DAC_X: U1.15, U1.17
  DAC_Y: U1.21, U1.23
  15V: U1.26, U1.35
  -15V: U1.28, U1.33
  Ref_XY: U1.30
  Ref_SP_I: U1.31
  DAC_Itunnel: U1.38, U1.40
  DAC_Setpoint: U1.44, U1.46
